# Fritzing sketch Particle and neopixel (saved by Fritzing 0.9.3b)
circuit board: 10.1863cm x 8.01549cm
breadboards: 1

parts:
  Neopixel = female pin header, 4 pins [form="♀ (female)"]
  J1 = female pin header, 5 pins [form="♀ (female)"]
  Part1 = Arduino Uno (Rev3)

nets:
  N1: Neopixel.pin1, J1.pin3, Part1.5V
  N2: Neopixel.pin2, Part1.D6_PWM
  N3: Neopixel.pin3, Neopixel.pin4, J1.pin2, Part1.GND
  N4: J1.pin4, Part1.A4/SDA
  N5: J1.pin5, Part1.A5/SCL
